# Fritzing sketch schematic (saved by Fritzing 0.9.5d)
stripboards: 1

parts:
  Raspberry_Pi_1 = Raspberry Pi 3 [part_number=RPI-3-V1.2]
  J19 = male pin header, 7 pins [form="♂ (male)"]
  J20 = male pin header, 7 pins [form="♂ (male)"]
  J21 = male pin header, 7 pins [form="♂ (male)"]
  J23 = male pin header, 7 pins [form="♂ (male)"]
  J22 = female pin header, 7 pins [form="♀ (female)"]

nets:
  N1: Raspberry_Pi_1.GPIO2, J19.pin7, J20.pin7, J21.pin7, J23.pin7, J22.pin7
  N2: Raspberry_Pi_1.GPIO3, J19.pin6, J20.pin6, J21.pin6, J23.pin6, J22.pin6
  N3: Raspberry_Pi_1.GPIO23, J19.pin1, J20.pin1, J21.pin1, J23.pin1, J22.pin1
  N4: Raspberry_Pi_1.GND, J19.pin4, J20.pin4, J21.pin4, J23.pin4, J22.pin4
  N5: Raspberry_Pi_1.5V, J19.pin5, J20.pin5, J21.pin5, J23.pin5, J22.pin5
  N6: J19.pin2, J20.pin2, J21.pin2, J23.pin2, J22.pin2
  N7: J19.pin3, J20.pin3, J21.pin3, J23.pin3, J22.pin3

notes:
  GND
  VCC
  SDA
  SCL
  GPIO
